# Fritzing sketch solar-power-system (saved by Fritzing 0.9.9b)
circuit board: 8.46667cm x 5.64444cm
breadboards: 2

parts:
  Bauteil1 = SparkFun ESP8266 Thing
  Bauteil3 = INA 260
  Bauteil4 = INA 260
  Bauteil5 = INA 260
  J1 = Screw terminal - 2 pins [package=THT]  # not connected
  J2 = Screw terminal - 2 pins [package=THT]  # not connected
  J3 = Screw terminal - 2 pins [package=THT]
  VCC1 = Battery

nets:
  GND: Bauteil1.GND, Bauteil3.GND, Bauteil4.GND, Bauteil5.GND, J3.pin2, VCC1.-
  VCC: Bauteil1.VCC, Bauteil3.VCC, Bauteil4.VCC, Bauteil5.VCC

custom parts:
  INA 260: Rev. B, add copy
